# Fritzing sketch callattendant-hat (saved by Fritzing 0.9.3b)
circuit board: 8.53488cm x 5.63626cm

parts:
  GRN = LED - 3mm [color="Green (555nm)" package="3 mm [THT]"]
  ORG = LED - 3mm [color="Orange (620nm)" package="3 mm [THT]"]
  BLU = LED - 3mm [color="Blue (525nm)" package="3 mm [THT]"]
  R2 = Resistor [tolerance=±5% resistance=15 package=THT]
  R3 = Resistor [tolerance=±5% resistance=56 package=THT]
  R4 = Resistor [tolerance=±5% resistance=56 package=THT]
  V1 = DC Power [voltage=5]  # not connected
  RED = LED - 3mm [color="Red (633nm)" package="3 mm [THT]"]
  R5 = Resistor [tolerance=±5% resistance=100 package=THT]  # not connected
  R6 = Resistor [tolerance=±5% resistance=100 package=THT]
  R7 = Resistor [tolerance=±5% resistance=100 package=THT]  # not connected
  R8 = Resistor [tolerance=±5% resistance=100 package=THT]
  R9 = Resistor [tolerance=±5% resistance=100 package=THT]
  R10 = Resistor [tolerance=±5% resistance=100 package=THT]
  R11 = Resistor [tolerance=±5% resistance=100 package=THT]
  R12 = Resistor [tolerance=±5% resistance=100 package=THT]
  RasPi_Proto_Board = Raspberry Pi Shield [width=85.348826 height=56.36259999999999]  # not connected
  R1 = Resistor [tolerance=±5% resistance=15 package=THT]  # not connected
  7_SEG_LED = mystery part, 14 pins [chip_label=Kingbright]

nets:
  N1: GRN.cathode, ORG.cathode, BLU.cathode, RED.cathode
  N2: GRN.anode, R2.Pin_1
  N3: BLU.anode, R3.Pin_1
  N4: R4.Pin_1, RED.anode
  N5: R6.Pin_1, 7_SEG_LED.pin6
  N6: R8.Pin_1, 7_SEG_LED.pin1
  N7: R9.Pin_1, 7_SEG_LED.pin13
  N8: R10.Pin_1, 7_SEG_LED.pin11
  N9: R11.Pin_1, 7_SEG_LED.pin10
  N10: R12.Pin_1, 7_SEG_LED.pin8

notes:
  7-SEG LED segments: a=1, b=13, c=10, d=8, e=7. f=2, g=11, dp=6

custom parts:
  Raspberry Pi Shield: Plain PCB Shaped to fit as Raspberry Pi B+ Hat
